// Logisim project Ula.circ as structural Verilog: 1 circuit, main circuit Somador
module Somador (
  input  Select__1,
  input  Select___0,
  input  Bit_Invert,
  input  carry_in,
  input  Clear,
  output s7,
  output s6,
  output s5,
  output s4,
  output s3,
  output s2,
  output s1,
  output s0
);

  wire and_1_out, and_2_out, and_3_out, and_4_out, and_5_out, and_6_out, and_7_out, and_8_out, and_9_out,
       and_10_out, Clock__tap_16_times_out, d_ff_1_q, d_ff_2_q, d_ff_4_q, d_ff_5_q, d_ff_7_q, d_ff_8_q,
       d_ff_10_q, d_ff_11_q, d_ff_13_q, d_ff_14_q, d_ff_16_q, d_ff_17_q, d_ff_19_q, d_ff_20_q, d_ff_22_q,
       d_ff_23_q, d_ff_25_q, not_1_out, not_2_out, not_3_out, not_4_out, not_5_out, or_1_out, or_2_out,
       or_3_out, or_4_out, or_5_out, xor_1_out, xor_2_out;

  Clock Clock__tap_16_times (.out(Clock__tap_16_times_out));
  D_Flip_Flop d_ff_1 (.clk(Clock__tap_16_times_out), .Q(d_ff_1_q), .reset(Clear));  // open: D, Qn, preset, en
  D_Flip_Flop d_ff_2 (.clk(Clock__tap_16_times_out), .Q(d_ff_2_q), .reset(Clear));  // open: D, Qn, preset, en
  D_Flip_Flop d_ff_3 (.clk(Clock__tap_16_times_out), .D(or_5_out), .Q(s7), .reset(Clear));  // open: Qn, preset, en
  D_Flip_Flop d_ff_4 (
    .clk(Clock__tap_16_times_out), .D(d_ff_1_q), .Q(d_ff_4_q), .reset(Clear));  // open: Qn, preset, en
  D_Flip_Flop d_ff_5 (
    .clk(Clock__tap_16_times_out), .D(d_ff_2_q), .Q(d_ff_5_q), .reset(Clear));  // open: Qn, preset, en
  D_Flip_Flop d_ff_6 (.clk(Clock__tap_16_times_out), .D(s7), .Q(s6), .reset(Clear));  // open: Qn, preset, en
  D_Flip_Flop d_ff_7 (
    .clk(Clock__tap_16_times_out), .D(d_ff_4_q), .Q(d_ff_7_q), .reset(Clear));  // open: Qn, preset, en
  D_Flip_Flop d_ff_8 (
    .clk(Clock__tap_16_times_out), .D(d_ff_5_q), .Q(d_ff_8_q), .reset(Clear));  // open: Qn, preset, en
  D_Flip_Flop d_ff_9 (.clk(Clock__tap_16_times_out), .D(s6), .Q(s5), .reset(Clear));  // open: Qn, preset, en
  D_Flip_Flop d_ff_10 (
    .clk(Clock__tap_16_times_out), .D(d_ff_7_q), .Q(d_ff_10_q), .reset(Clear));  // open: Qn, preset, en
  D_Flip_Flop d_ff_11 (
    .clk(Clock__tap_16_times_out), .D(d_ff_8_q), .Q(d_ff_11_q), .reset(Clear));  // open: Qn, preset, en
  D_Flip_Flop d_ff_12 (.clk(Clock__tap_16_times_out), .D(s5), .Q(s4), .reset(Clear));  // open: Qn, preset, en
  D_Flip_Flop d_ff_13 (
    .clk(Clock__tap_16_times_out), .D(d_ff_10_q), .Q(d_ff_13_q), .reset(Clear));  // open: Qn, preset, en
  D_Flip_Flop d_ff_14 (
    .clk(Clock__tap_16_times_out), .D(d_ff_11_q), .Q(d_ff_14_q), .reset(Clear));  // open: Qn, preset, en
  D_Flip_Flop d_ff_15 (.clk(Clock__tap_16_times_out), .D(s4), .Q(s3), .reset(Clear));  // open: Qn, preset, en
  D_Flip_Flop d_ff_16 (
    .clk(Clock__tap_16_times_out), .D(d_ff_13_q), .Q(d_ff_16_q), .reset(Clear));  // open: Qn, preset, en
  D_Flip_Flop d_ff_17 (
    .clk(Clock__tap_16_times_out), .D(d_ff_14_q), .Q(d_ff_17_q), .reset(Clear));  // open: Qn, preset, en
  D_Flip_Flop d_ff_18 (.clk(Clock__tap_16_times_out), .D(s3), .Q(s2), .reset(Clear));  // open: Qn, preset, en
  D_Flip_Flop d_ff_19 (
    .clk(Clock__tap_16_times_out), .D(d_ff_16_q), .Q(d_ff_19_q), .reset(Clear));  // open: Qn, preset, en
  D_Flip_Flop d_ff_20 (
    .clk(Clock__tap_16_times_out), .D(d_ff_17_q), .Q(d_ff_20_q), .reset(Clear));  // open: Qn, preset, en
  D_Flip_Flop d_ff_21 (.clk(Clock__tap_16_times_out), .D(s2), .Q(s1), .reset(Clear));  // open: Qn, preset, en
  D_Flip_Flop d_ff_22 (
    .clk(Clock__tap_16_times_out), .D(d_ff_19_q), .Q(d_ff_22_q), .reset(Clear));  // open: Qn, preset, en
  D_Flip_Flop d_ff_23 (
    .clk(Clock__tap_16_times_out), .D(d_ff_20_q), .Q(d_ff_23_q), .reset(Clear));  // open: Qn, preset, en
  D_Flip_Flop d_ff_24 (.clk(Clock__tap_16_times_out), .D(s1), .Q(s0), .reset(Clear));  // open: Qn, preset, en
  not not_1 (not_1_out, carry_in);
  and and_1 (and_1_out, carry_in, carry_in);
  and and_2 (and_2_out, not_1_out, d_ff_25_q);
  or or_1 (or_1_out, and_1_out, and_2_out);
  D_Flip_Flop d_ff_25 (
    .clk(Clock__tap_16_times_out), .D(or_4_out), .Q(d_ff_25_q), .reset(Clear));  // open: Qn, preset, en
  not not_2 (not_2_out, d_ff_23_q);
  not not_3 (not_3_out, Bit_Invert);
  and and_3 (and_3_out, not_2_out, Bit_Invert);
  and and_4 (and_4_out, not_3_out, d_ff_23_q);
  or or_2 (or_2_out, and_3_out, and_4_out);
  and and_5 (and_5_out, d_ff_22_q, or_2_out);
  or or_3 (or_3_out, d_ff_22_q, or_2_out);
  xor xor_1 (xor_1_out, d_ff_22_q, or_2_out);
  xor xor_2 (xor_2_out, xor_1_out, or_1_out);
  and and_6 (and_6_out, or_1_out, xor_1_out);
  and and_7 (and_7_out, d_ff_22_q, or_2_out);
  or or_4 (or_4_out, and_6_out, and_7_out);
  not not_4 (not_4_out, Select__1);
  not not_5 (not_5_out, Select___0);
  and and_8 (and_8_out, and_5_out, not_4_out, not_5_out);
  and and_9 (and_9_out, or_3_out, not_4_out, Select___0);
  and and_10 (and_10_out, xor_2_out, Select__1, not_5_out);
  or or_5 (or_5_out, and_8_out, and_9_out, and_10_out);

  // Notes on the sheet:
  //   A
  //   B
  //   A
  //   B
  //   somador in a
  //   somador in b
  //   somador carry in
  //   Select 1
  //   somador out
  //   Select 0
  //   somador carry out
  //   D0
  //   D1
  //   D2
endmodule
